# Fritzing sketch CNMB3-B (saved by Fritzing 0.9.8b)
circuit board: 4.9cm x 5.7cm
breadboards: 1

parts:
  LED1 = LED - 5mm [color="Red (633nm)" current=0.030 package="5 mm [THT]"]
  LED2 = LED - 5mm [color="Red (633nm)" current=0.030 package="5 mm [THT]"]
  IC1 = IC, DIP package, 16 pins [chip_label=IC]
  J10 = double row female pin header, 8 pins [form="♀ (female)"]
  Q1 = NPN-Transistor [package="TO92 [THT]"]
  D1 = Rectifier Diode [part_number=1N4001 package="300 mil [THT]"]
  R2 = Resistor [tolerance=±5% power=0.25 resistance=220 package=THT]

nets:
  N1: LED1.cathode, LED2.cathode, J10.pin8, Q1.E
  N2: LED1.anode, J10.pin2
  N3: LED2.anode, J10.pin7
  N4: IC1.pin8, Q1.C, D1.anode
  N5: IC1.pin9, J10.pin1, D1.cathode
  N6: IC1.pin12, J10.pin4
  N7: IC1.pin14, J10.pin5
  N8: IC1.pin16, J10.pin3
  N9: J10.pin6, R2.Pin_1
  N10: Q1.B, R2.Pin_0

notes:
  POWER
  ERROR
  DOMOTA
  by cone
  C A 3 5
  B D E 0
  --
